# Fritzing sketch pirthing (saved by Fritzing 0.9.4)
breadboards: 1

parts:
  Part1 = USB Mini-B Breakout [part_number=1764]
  Part2 = Adafruit HUZZAH ESP8266 [part_number="Adafruit #2471"]
  PIR1 = PIR sensor
  LED1 = LED - 3mm [color="Red (633nm)" package="3 mm [THT]"]
  R1 = Resistor [tolerance=±5% resistance=220 package=THT]

nets:
  GND: Part1.GND, Part2.GND, PIR1.GND, R1.Pin_0
  5V: Part1.5V, Part2.VIN, PIR1.VDD
  N1: Part2.GPIO16, PIR1.SIG
  N2: Part2.GPIO13, LED1.anode
  N3: LED1.cathode, R1.Pin_1

custom parts:
  USB Mini-B Breakout: Simple but effective - this breakout board has a USB Mini-B connector, with all 5 pins broken out. Great for pairing with a microcontroller with USB support, or adding USB 5V power to a project.
  Adafruit HUZZAH ESP8266: Add Internet to your next project with an adorable, bite-sized WiFi microcontroller, at a price you like! The ESP8266 processor from Espressif is an 80 MHz microcontroller with a full WiFi front-end (both as client and access point) and TCP/IP stack with DNS support as well. While this chip has been very popular, its also been very difficult to use. Most of the low cost modules are not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
